// Logisim project BRM.circ as structural Verilog: 2 circuits, main circuit brm0
module brm0 (
  input  [15:0] OperationCode,
  input  [15:0] Operand,
  input  Clock
);

  wire dcode_1_a, dcode_1_b, dcode_1_c, dcode_1_d, dcode_1_e, dcode_1_f, dcode_1_g, dcode_1_h, dcode_2_e,
       dcode_2_f, dcode_2_g, dcode_2_h, dcode_3_a, dcode_3_b, dcode_3_c, dcode_3_d, dcode_3_e, dcode_3_f,
       dcode_3_g, dcode_3_h, LDX, LDY, LXY, SWP, WRITE, WRX, WRY, XTY;
  wire [15:0] dcode_2_checkcarry, dcode_2_comparedcarry, RX, RY, undriven, undriven_2, WXV, WYV;

  dCode dcode_1 (
    .Compared(undriven), .Check(undriven_2), .A(dcode_1_a), .B(dcode_1_b), .C(dcode_1_c), .D(dcode_1_d),
    .E(dcode_1_e), .F(dcode_1_f), .G(dcode_1_g), .H(dcode_1_h));  // open: ComparedCarry, CheckCarry
  Register #(.width(16)) X (.D(WXV), .en(WRX), .Q(RX), .clk(Clock), .clr(1'b0));
  dCode dcode_2 (
    .Compared(OperationCode), .Check({16{1'b0}}), .ComparedCarry(dcode_2_comparedcarry),
    .CheckCarry(dcode_2_checkcarry), .A(LDX), .B(LDY), .C(SWP), .D(LXY), .E(dcode_2_e), .F(dcode_2_f),
    .G(dcode_2_g), .H(dcode_2_h));
  dCode dcode_3 (
    .Compared(dcode_2_comparedcarry), .Check(dcode_2_checkcarry), .A(dcode_3_a), .B(dcode_3_b),
    .C(dcode_3_c), .D(dcode_3_d), .E(dcode_3_e), .F(dcode_3_f), .G(dcode_3_g), .H(dcode_3_h));  // open: ComparedCarry, CheckCarry
  Register #(.width(16)) Y (.D(WYV), .en(WRY), .Q(RY), .clk(Clock), .clr(1'b0));
  or or_1 (XTY, LXY, SWP);
  Multiplexer #(.width(16)) multiplexer_1 (.in0(Operand), .in1(RY), .out(WXV), .sel(XTY));
  Multiplexer #(.width(16)) multiplexer_2 (.in0(Operand), .in1(RX), .out(WYV), .sel(SWP));
  or or_2 (WRX, LDX, XTY);
  or or_3 (WRY, LDY, SWP);
  or or_4 (WRITE, WRX, WRY);

  // Other names for the same wires on the sheet: OPCODE[15:0] = OperationCode

  // Notes on the sheet:
  //   dont touch
endmodule

module dCode (
  input  [15:0] Compared,
  input  [15:0] Check,
  output A,
  output B,
  output C,
  output D,
  output E,
  output F,
  output G,
  output H,
  output [15:0] ComparedCarry,
  output [15:0] CheckCarry
);

  wire [15:0] adder_1_out, adder_2_out, adder_3_out, adder_4_out, adder_5_out, adder_6_out, adder_7_out;

  Adder #(.width(16)) adder_1 (.a(16'h1), .b(Check), .out(adder_1_out));  // open: cin, cout
  Adder #(.width(16)) adder_2 (.a(16'h1), .b(adder_1_out), .out(adder_2_out));  // open: cin, cout
  Adder #(.width(16)) adder_3 (.a(16'h1), .b(adder_2_out), .out(adder_3_out));  // open: cin, cout
  Adder #(.width(16)) adder_4 (.a(16'h1), .b(adder_3_out), .out(adder_4_out));  // open: cin, cout
  Adder #(.width(16)) adder_5 (.a(16'h1), .b(adder_4_out), .out(adder_5_out));  // open: cin, cout
  Adder #(.width(16)) adder_6 (.a(16'h1), .b(adder_5_out), .out(adder_6_out));  // open: cin, cout
  Adder #(.width(16)) adder_7 (.a(16'h1), .b(adder_6_out), .out(adder_7_out));  // open: cin, cout
  Adder #(.width(16)) adder_8 (.a(16'h1), .b(adder_7_out), .out(CheckCarry));  // open: cin, cout
  Comparator #(.width(16)) comparator_1 (.a(Compared), .b(Check), .eq(A));  // open: gt, lt
  Comparator #(.width(16)) comparator_2 (.a(Compared), .b(adder_1_out), .eq(B));  // open: gt, lt
  Comparator #(.width(16)) comparator_3 (.a(Compared), .b(adder_2_out), .eq(C));  // open: gt, lt
  Comparator #(.width(16)) comparator_4 (.a(Compared), .b(adder_3_out), .eq(D));  // open: gt, lt
  Comparator #(.width(16)) comparator_5 (.a(Compared), .b(adder_4_out), .eq(E));  // open: gt, lt
  Comparator #(.width(16)) comparator_6 (.a(Compared), .b(adder_5_out), .eq(F));  // open: gt, lt
  Comparator #(.width(16)) comparator_7 (.a(Compared), .b(adder_6_out), .eq(G));  // open: gt, lt
  Comparator #(.width(16)) comparator_8 (.a(Compared), .b(adder_7_out), .eq(H));  // open: gt, lt

  assign ComparedCarry = Compared;
endmodule
